# Fritzing sketch Vib (saved by Fritzing 0.9.3b)

parts:
  Part1 = Arduino Uno (Rev3)
  e-radionica_com1 = LM393 vibration sensor breakout [part_number=100031]
  LED1 = smd LED [color="Red (633nm)" package="0603 [SMD]"]
  SG1 = Buzzer 12mm [package=buzzer-ccv-kit]

nets:
  GND: Part1.GND, e-radionica_com1.GND, SG1.1
  N1: Part1.D3_PWM, e-radionica_com1.DO
  N2: Part1.D5_PWM, LED1.anode
  N3: Part1.D6_PWM, SG1.2
  5V: Part1.5V, e-radionica_com1.VCC
